// Logisim project encodeur_octal.circ as structural Verilog: 1 circuit, main circuit main
module main (
  input  e1,
  input  e2,
  input  e3,
  input  e4,
  input  e5,
  input  e6,
  input  e7,
  input  e0,
  output out_9,
  output out_10,
  output out_11
);

  or or_1 (out_9, e4, e5, e6, e7);
  or or_2 (out_10, e2, e3, e6, e7);
  or or_3 (out_11, e1, e3, e5, e7);
endmodule
