// Logisim project NZP.circ as structural Verilog: 1 circuit, main circuit main
module main (
  input  [15:0] RES,
  output [2:0] NZP
);

  wire not_2_out, or_1_out;

  or or_1 (or_1_out, RES[0], RES[1], RES[2], RES[3], RES[4], RES[5], RES[6], RES[7], RES[8], RES[9], RES[10], RES[11], RES[12], RES[13], RES[14], RES[15]);
  and and_1 (NZP[0], or_1_out, not_2_out);
  not not_1 (NZP[1], or_1_out);
  not not_2 (not_2_out, RES[15]);

  assign NZP[2] = RES[15];
endmodule
