// Logisim project encodeur_octal.circ as structural Verilog: 1 circuit, main circuit main
module main (
  input  e0,
  input  e1,
  input  e2,
  input  e3,
  input  e4,
  input  e5,
  input  e6,
  input  e7,
  output s0,
  output s1,
  output s2
);

  or or_1 (s0, e1, e3, e5, e7);
  or or_2 (s1, e2, e3, e6, e7);
  or or_3 (s2, e4, e5, e6, e7);
endmodule
