// Logisim project encodeur_octale.circ as structural Verilog: 1 circuit, main circuit main
module main (
  input  [7:0] in_1,
  input  in_2,
  input  [7:0] in_3,
  output [3:0] out_4
);

  wire [3:0] adder_1_out, adder_2_out;

  Adder #(.width(4)) adder_1 (.a(in_1[3:0]), .b(in_3[3:0]), .out(adder_1_out));  // open: cin, cout
  Adder #(.width(4)) adder_2 (.a(in_1[7:4]), .b(in_3[7:4]), .out(adder_2_out));  // open: cin, cout
  Multiplexer #(.width(4)) multiplexer_1 (.in0(adder_1_out), .in1(adder_2_out), .out(out_4), .sel(in_2));  // open: en
endmodule
