// Logisim project exo3.circ as structural Verilog: 2 circuits, main circuit main
module main (
  input  [7:0] in_1,
  output [15:0] out_2
);


  assign out_2 = {{9{in_1[7]}}, in_1[6:0]};
endmodule

module brouillon (
  input  [7:0] in_1,
  output [15:0] out_2
);

  assign out_2 = {{8{in_1[7]}}, in_1};  // Bit_Extender bit_extender_1
endmodule
