// Logisim project exo4_tp3.circ as structural Verilog: 2 circuits, main circuit main
module main (
  input  [7:0] in_1,
  input  [7:0] in_2,
  output [15:0] out_3,
  output [15:0] out_4
);

  assign out_4 = {{8{1'b0}}, in_2};  // Bit_Extender bit_extender_1
  Bit_Extender #(.in_width(6)) bit_extender_2 ();  // open: in, out
endmodule

module brouillon (
  input  [7:0] in_1,
  output [15:0] out_2
);


  assign out_2 = {{9{in_1[7]}}, in_1[6:0]};
endmodule
