// Logisim project ram.circ as structural Verilog: 1 circuit, main circuit main
module main (
  input  [3:0] in_1,
  input  in_2,
  output [7:0] out_3
);

  wire clock_1_out;

  Clock clock_1 (.out(clock_1_out));
  RAM #(.addrWidth(4)) ram_1 (.addr(in_1), .data(out_3), .clk(clock_1_out), .ld(in_2));  // open: sel, clr
endmodule
