// Logisim project ram_2.circ as structural Verilog: 1 circuit, main circuit main
module main (
  input  [7:0] in_1,
  input  in_2,
  input  [3:0] in_3,
  input  [7:0] in_4
);

  wire clock_1_out, not_1_out;

  assign in_4 = in_2 ? in_1 : 8'bz;  // Controlled_Buffer controlled_buffer_1
  not not_1 (not_1_out, in_2);
  RAM #(.addrWidth(4)) ram_1 (.addr(in_3), .data(in_4), .clk(clock_1_out), .ld(not_1_out));  // open: sel, clr
  Clock clock_1 (.out(clock_1_out));
endmodule
