// Logisim project ram_3.circ as structural Verilog: 1 circuit, main circuit main
module main (
  input  [7:0] in_1,
  input  in_2,
  input  [3:0] in_3
);

  wire clock_1_out, not_1_out;
  wire [7:0] controlled_buffer_1_out;

  assign controlled_buffer_1_out = in_2 ? in_1 : 8'bz;  // Controlled_Buffer controlled_buffer_1
  not not_1 (not_1_out, in_2);
  RAM #(.addrWidth(4)) ram_1 (
    .addr(in_3), .data(controlled_buffer_1_out), .clk(clock_1_out), .ld(not_1_out));  // open: sel, clr
  Clock clock_1 (.out(clock_1_out));
  Hex_Digit_Display hex_digit_display_1 (.value(controlled_buffer_1_out[7:4]));  // open: dp
  Hex_Digit_Display hex_digit_display_2 (.value(controlled_buffer_1_out[3:0]));  // open: dp
endmodule
