// Logisim project ram_4.circ as structural Verilog: 2 circuits, main circuit main
module main (
  input  [7:0] in_1,
  input  in_2
);

  wire clock_1_out, not_1_out;
  wire [3:0] compteur_1_out_1;
  wire [7:0] controlled_buffer_1_out;

  compteur compteur_1 (.out_1(compteur_1_out_1));
  assign controlled_buffer_1_out = in_2 ? in_1 : 8'bz;  // Controlled_Buffer controlled_buffer_1
  not not_1 (not_1_out, in_2);
  RAM #(.addrWidth(4)) ram_1 (
    .addr(compteur_1_out_1), .data(controlled_buffer_1_out), .clk(clock_1_out), .ld(not_1_out));  // open: sel, clr
  Clock clock_1 (.out(clock_1_out));
  Hex_Digit_Display hex_digit_display_1 (.value(controlled_buffer_1_out[7:4]));  // open: dp
  Hex_Digit_Display hex_digit_display_2 (.value(controlled_buffer_1_out[3:0]));  // open: dp
endmodule

module compteur (
  output [3:0] out_1
);

  wire clock_1_out;
  wire [3:0] adder_1_out;

  Adder #(.width(4)) adder_1 (.a(out_1), .b(4'b0001), .out(adder_1_out));  // open: cin, cout
  Register #(.width(4)) register_1 (.D(adder_1_out), .Q(out_1), .clk(clock_1_out));  // open: en, clr
  Clock clock_1 (.out(clock_1_out));
endmodule
