// Logisim project tp4_cpt4.circ as structural Verilog: 1 circuit, main circuit cpt4
module cpt4 (
  input  [3:0] in_1,
  output out_2,
  output halt,
  output [3:0] halt_2,
  output [3:0] out_5
);

  wire clock_1_out, clock_2_out;
  wire [3:0] adder_1_out;

  and and_1 (halt, out_5[3], out_5[2], out_5[1], out_5[0]);
  Clock clock_1 (.out(clock_1_out));
  D_Flip_Flop d_ff_1 (.clk(clock_1_out), .D(adder_1_out[3]), .Q(out_5[3]));  // open: Qn, preset, en, reset
  D_Flip_Flop d_ff_2 (.clk(clock_1_out), .D(adder_1_out[2]), .Q(out_5[2]));  // open: Qn, preset, en, reset
  D_Flip_Flop d_ff_3 (.clk(clock_1_out), .D(adder_1_out[1]), .Q(out_5[1]));  // open: Qn, preset, en, reset
  D_Flip_Flop d_ff_4 (.clk(clock_1_out), .D(adder_1_out[0]), .Q(out_5[0]));  // open: Qn, preset, en, reset
  Comparator #(.width(4)) comparator_1 (.a(out_5), .b(halt_2), .eq(out_2));  // open: gt, lt
  Adder #(.width(4)) adder_1 (.a(4'b0000), .b(out_5), .out(adder_1_out), .cin(1'b1));  // open: cout
  Clock clock_2 (.out(clock_2_out));
  Counter #(.width(4), .max('hf)) counter_1 (.D(in_1), .Q(halt_2), .clk(clock_2_out));  // open: load, count, carry, clr

  // Notes on the sheet:
  //   valeur courante
  //   Compteur 4 bits
endmodule
