// Logisim project additionneur.circ as structural Verilog: 2 circuits, main circuit main
module main (
  input  in_1,
  input  in_2,
  input  in_3,
  input  in_4,
  input  in_5,
  input  in_6,
  input  in_7,
  input  in_8,
  input  in_9,
  input  in_10,
  input  in_11,
  output out_12,
  output out_13,
  output out_14,
  output out_15,
  output out_16,
  output [7:0] out_17,
  output out_18,
  output out_19
);

  wire add_2_out_4, add_3_out_4, add_4_out_4;
  wire [7:0] subtractor_1_out;

  add add_1 (.out_4(out_12), .e0(in_1), .e1(in_2), .out_5(out_13), .in_3(add_2_out_4));
  add add_2 (.out_4(add_2_out_4), .e0(in_3), .e1(in_4), .out_5(out_14), .in_3(add_3_out_4));
  Adder adder_1 (.a({8{1'b1}}), .b({8{1'b1}}), .out(out_17), .cin(in_10), .cout(out_18));
  Subtractor subtractor_1 (.a({8{1'b1}}), .b({8{1'b1}}), .out(subtractor_1_out), .bin(in_11), .bout(out_19));
  add add_3 (.out_4(add_3_out_4), .e0(in_5), .e1(in_6), .out_5(out_15), .in_3(add_4_out_4));
  add add_4 (.out_4(add_4_out_4), .e0(in_7), .e1(in_8), .out_5(out_16), .in_3(in_9));
endmodule

module add (
  input  e0,
  input  e1,
  input  in_3,
  output out_4,
  output out_5
);

  wire and_1_out, and_2_out, xor_1_out;

  or or_1 (out_4, and_1_out, and_2_out);
  and and_1 (and_1_out, e0, e1);
  and and_2 (and_2_out, xor_1_out, in_3);
  xor xor_1 (xor_1_out, e0, e1);
  xor xor_2 (out_5, xor_1_out, in_3);
endmodule
