// Logisim project decodeurs.circ as structural Verilog: 1 circuit, main circuit main
module main (
  input  in_1,
  input  in_2,
  input  in_3,
  input  [2:0] in_4,
  output out_5,
  output out_6,
  output out_7,
  output out_8,
  output out_9,
  output out_10,
  output out_11,
  output out_12,
  output [7:0] out_13
);

  wire not_1_out, not_2_out, not_3_out;

  not not_1 (not_1_out, in_1);
  not not_2 (not_2_out, in_2);
  not not_3 (not_3_out, in_3);
  Decoder #(.select(3)) decoder_1 (
    .out0(out_13[0]), .out1(out_13[1]), .out2(out_13[2]), .out3(out_13[3]), .out4(out_13[4]),
    .out5(out_13[5]), .out6(out_13[6]), .out7(out_13[7]), .sel(in_4));  // open: en
  and and_1 (out_5, in_1, in_2, in_3);
  and and_2 (out_6, in_1, in_2, not_3_out);
  and and_3 (out_7, in_1, not_2_out, in_3);
  and and_4 (out_8, not_1_out, in_2, not_3_out);
  and and_5 (out_9, not_1_out, not_2_out, in_3);
  and and_6 (out_10, not_1_out, not_2_out, in_3);
  and and_7 (out_11, not_1_out, not_2_out, in_3);
  and and_8 (out_12, not_1_out, not_2_out, not_3_out);
endmodule
