// Logisim project multiplexeur.circ as structural Verilog: 1 circuit, main circuit main
module main (
  input  e0,
  input  e1,
  input  in_3,
  input  in_4,
  input  in_5,
  input  \bit_de_sélection ,
  output out_7,
  output out_8
);

  wire and_1_out, and_2_out, not_1_out;

  not not_1 (not_1_out, \bit_de_sélection );
  and and_1 (and_1_out, e0, not_1_out);
  and and_2 (and_2_out, e1, \bit_de_sélection );
  or or_1 (out_7, and_1_out, and_2_out);
  Multiplexer multiplexer_1 (.in0(in_3), .in1(in_4), .out(out_8), .sel(in_5));  // open: en
endmodule
