// Logisim project nzp.circ as structural Verilog: 1 circuit, main circuit main
module main (
  input  [15:0] RES,
  output [2:0] NZP
);

  wire not_2_out, xor_1_out;

  ExactlyOne xor_1 (
    .out(xor_1_out), .in0(RES[0]), .in1(RES[1]), .in2(RES[2]), .in3(RES[3]), .in4(RES[4]), .in5(RES[5]),
    .in6(RES[6]), .in7(RES[7]), .in8(RES[8]), .in9(RES[9]), .in10(RES[10]), .in11(RES[11]), .in12(RES[12]),
    .in13(RES[13]), .in14(RES[14]), .in15(RES[15]));
  and and_1 (NZP[0], not_2_out, xor_1_out);
  not not_1 (NZP[1], xor_1_out);
  not not_2 (not_2_out, RES[15]);

  assign NZP[2] = RES[15];
endmodule
